// Logisim project s-mips.circ as structural Verilog
module S_MIPS_Board (
  input  DESHABILITAR_DISPATCHER,
  output halt
);

  wire button_1_out, CLK, CS, d_ff_1_q, LCLR, LoadRAM, LoadRAMOn, LW, R_R_W, R_W, ram_dispatcher_1_finished,
       RCS, Reset_out, RST, TTY_EN;
  wire [2:0] KDB;
  wire [3:0] LMask, Mask, ram_1_read_time, ram_1_write_time, RMask;
  wire [6:0] KDB_DATA, TTY_DATA;
  wire [15:0] Addr, LAddr, RAddr;
  wire [31:0] I0, I1, I2, I3, LData, ram_1_data_out_0, ram_1_data_out_1, ram_1_data_out_2, ram_1_data_out_3,
       RI0, RI1, RI2, RI3;

  TTY #(.rows(25), .cols(80)) tty_1 (.data(TTY_DATA), .clk(CLK), .we(TTY_EN), .clr(RST));
  not not_1 (LoadRAMOn, ram_dispatcher_1_finished);
  RAM_Dispatcher ram_dispatcher_1 (
    .WriteTime(ram_1_write_time), .Clock(CLK), .Data(LData), .Address(LAddr), .Mask(LMask),
    .Finished(ram_dispatcher_1_finished), .Write(LW), .CLR(LCLR));
  Keyboard #(.buflen(64)) keyboard_1 (.clk(CLK), .re(KDB[0]), .avail(KDB[2]), .data(KDB_DATA));  // open: clr
  RAM ram_1 (
    .Address(RAddr), .Data_Out_0(ram_1_data_out_0), .Data_Out_1(ram_1_data_out_1),
    .Data_Out_2(ram_1_data_out_2), .Data_Out_3(ram_1_data_out_3), .Data_In_0(RI0), .Data_In_1(RI1),
    .Data_In_2(RI2), .Data_In_3(RI3), .Mask(RMask), .nRead_Write(R_R_W), .Chip_Select(RCS),
    .Read_Time(ram_1_read_time), .Reset(button_1_out), .Write_Time(ram_1_write_time));
  Button button_1 (.out(button_1_out));
  D_Flip_Flop d_ff_1 (.clk(CLK), .D(1'b1), .Q(d_ff_1_q), .reset(Reset_out));  // open: Qn, preset, en
  Button Reset (.out(Reset_out));
  S_MIPS s_mips_1 (
    .Kbd_Enable(KDB[0]), .Address(Addr), .Kbd_Clear(KDB[1]), .Kbd_Available(KDB[2]), .RAM_In_0(I0),
    .Kbd_ASCII_Data(KDB_DATA), .RAM_In_1(I1), .TTY_Enable(TTY_EN), .RAM_In_2(I2), .RAM_In_3(I3),
    .TTY_ASCII_Data(TTY_DATA), .Reset(RST), .RAM_Out_0(ram_1_data_out_0), .Clock(CLK),
    .RAM_Out_1(ram_1_data_out_1), .Stop(halt), .RAM_Out_2(ram_1_data_out_2), .RAM_Out_3(ram_1_data_out_3),
    .Mask(Mask), .Read_Time(ram_1_read_time), .Write_Time(ram_1_write_time), .nRead_Write(R_W),
    .Chip_Select(CS));
  D_Flip_Flop d_ff_2 (.clk(CLK), .D(d_ff_1_q), .Qn(LCLR), .reset(Reset_out));  // open: Q, preset, en
  or or_1 (RST, LCLR, LoadRAM);
  Clock clock_1 (.out(CLK));
  Multiplexer #(.width(32), .enable("false")) multiplexer_1 (.in0(I0), .in1(LData), .out(RI0), .sel(LoadRAM));
  Multiplexer #(.width(32), .enable("false")) multiplexer_2 (.in0(I1), .in1(LData), .out(RI1), .sel(LoadRAM));
  Multiplexer #(.width(32), .enable("false")) multiplexer_3 (.in0(I2), .in1(LData), .out(RI2), .sel(LoadRAM));
  Multiplexer #(.width(32), .enable("false")) multiplexer_4 (.in0(I3), .in1(LData), .out(RI3), .sel(LoadRAM));
  and and_1 (LoadRAM, ~DESHABILITAR_DISPATCHER, LoadRAMOn);  // AND_Gate
  Multiplexer #(.width(16), .enable("false")) multiplexer_5 (.in0(Addr), .in1(LAddr), .out(RAddr), .sel(LoadRAM));
  Multiplexer #(.width(4), .enable("false")) multiplexer_6 (.in0(Mask), .in1(LMask), .out(RMask), .sel(LoadRAM));
  Multiplexer #(.enable("false")) multiplexer_7 (.in0(CS), .in1(LW), .out(RCS), .sel(LoadRAM));
  Multiplexer #(.enable("false")) multiplexer_8 (.in0(R_W), .in1(LW), .out(R_R_W), .sel(LoadRAM));

  // Notes on the sheet:
  //   NO MODIFICAR
  //   Keyboard
endmodule

module RAM (
  input  [15:0] Address,
  input  [31:0] Data_In_0,
  input  [31:0] Data_In_1,
  input  [31:0] Data_In_2,
  input  [31:0] Data_In_3,
  input  [3:0] Mask,
  input  nRead_Write,
  input  Chip_Select,
  input  Reset,
  output [31:0] Data_Out_0,
  output [31:0] Data_Out_1,
  output [31:0] Data_Out_2,
  output [31:0] Data_Out_3,
  output [3:0] Read_Time,
  output [3:0] Write_Time
);

  wire and_2_out, and_3_out, and_4_out, and_5_out, and_6_out, and_7_out, and_8_out, and_9_out, Changed, CLK,
       comparator_2_eq, comparator_3_eq, comparator_4_eq, comparator_5_eq, comparator_6_eq, Count,
       demultiplexer_3_out0, Idle, Idle_q, Load, Load0, Load1, nand_1_out, or_1_out, or_2_out, or_3_out,
       or_4_out, or_5_out, or_6_out, or_7_out, or_8_out, or_9_out, or_10_out, Proc_q, Update_Mem, Zero_Time;
  wire [3:0] counter_1_q, multiplexer_1_out, subtractor_1_out;
  wire [31:0] register_1_q, register_2_q, register_3_q, register_4_q, register_5_q;

  // Probe on 4'b0011
  // Probe on 4'b0010
  Multiplexer #(.width(4), .enable("false")) multiplexer_1 (
    .in0(4'b0011), .in1(4'b0010), .out(multiplexer_1_out), .sel(nRead_Write));
  or or_1 (or_1_out, Idle, Update_Mem);
  or or_2 (or_2_out, ~Chip_Select, Reset);  // OR_Gate
  Subtractor #(.width(4)) subtractor_1 (.a(multiplexer_1_out), .b(4'b0010), .out(subtractor_1_out));  // open: bin, bout
  Demultiplexer #(.enable("false")) demultiplexer_1 (.out0(Idle), .out1(Load0), .in(Idle_q), .sel(Changed));
  D_Flip_Flop u_Idle (.clk(CLK), .D(or_1_out), .Q(Idle_q), .preset(or_2_out));  // open: Qn, en, reset
  // Probe on counter_1_q
  Counter #(.width(4), .max('hf)) counter_1 (
    .load(Load), .D(subtractor_1_out), .count(Count), .Q(counter_1_q), .clk(CLK), .clr(or_3_out));  // open: carry
  or or_3 (or_3_out, ~Chip_Select, Reset);  // OR_Gate
  Comparator #(.width(4), .mode("unsigned")) comparator_1 (
    .a(4'b0000), .b(counter_1_q), .eq(Zero_Time));  // open: gt, lt
  or or_4 (or_4_out, Count, Load0, Load1);
  Register #(.width(32)) register_1 (.D(Data_In_0), .en(Chip_Select), .Q(register_1_q), .clk(CLK), .clr(or_5_out));
  or or_5 (or_5_out, ~Chip_Select, Reset);  // OR_Gate
  Register #(.width(32)) register_2 (.D(Data_In_1), .en(Chip_Select), .Q(register_2_q), .clk(CLK), .clr(or_6_out));
  or or_6 (or_6_out, ~Chip_Select, Reset);  // OR_Gate
  Register #(.width(32)) register_3 (.D(Data_In_2), .en(Chip_Select), .Q(register_3_q), .clk(CLK), .clr(or_7_out));
  or or_7 (or_7_out, ~Chip_Select, Reset);  // OR_Gate
  Register #(.width(32)) register_4 (.D(Data_In_3), .en(Chip_Select), .Q(register_4_q), .clk(CLK), .clr(or_8_out));
  or or_8 (or_8_out, ~Chip_Select, Reset);  // OR_Gate
  Register #(.width(32)) register_5 (
    .D({{11{1'b1}}, nRead_Write, Mask, Address}), .en(Chip_Select), .Q(register_5_q), .clk(CLK),
    .clr(or_9_out));
  or or_9 (or_9_out, ~Chip_Select, Reset);  // OR_Gate
  D_Flip_Flop Proc (.clk(CLK), .D(or_4_out), .Q(Proc_q), .reset(or_10_out));  // open: Qn, preset, en
  or or_10 (or_10_out, ~Chip_Select, Reset);  // OR_Gate
  Demultiplexer #(.enable("false")) demultiplexer_2 (
    .out0(Count), .out1(Update_Mem), .in(demultiplexer_3_out0), .sel(Zero_Time));
  Demultiplexer #(.enable("false")) demultiplexer_3 (
    .out0(demultiplexer_3_out0), .out1(Load1), .in(Proc_q), .sel(Changed));
  Clock clock_1 (.out(CLK));
  Comparator #(.width(32)) comparator_2 (.a(register_1_q), .b(Data_In_0), .eq(comparator_2_eq));  // open: gt, lt
  Comparator #(.width(32)) comparator_3 (.a(register_2_q), .b(Data_In_1), .eq(comparator_3_eq));  // open: gt, lt
  Comparator #(.width(32)) comparator_4 (.a(register_3_q), .b(Data_In_2), .eq(comparator_4_eq));  // open: gt, lt
  Comparator #(.width(32)) comparator_5 (.a(register_4_q), .b(Data_In_3), .eq(comparator_5_eq));  // open: gt, lt
  Comparator #(.width(32)) comparator_6 (
    .a(register_5_q), .b({{11{1'b1}}, nRead_Write, Mask, Address}), .eq(comparator_6_eq));  // open: gt, lt
  nand nand_1 (nand_1_out, comparator_6_eq, comparator_2_eq, comparator_3_eq, comparator_4_eq, comparator_5_eq);
  and and_1 (Changed, nand_1_out, Chip_Select);
  or or_11 (Load, Count, Load1, Load0);
  and and_2 (and_2_out, Mask[0], Update_Mem, nRead_Write);
  and and_3 (and_3_out, Mask[1], Update_Mem, nRead_Write);
  and and_4 (and_4_out, Mask[2], Update_Mem, nRead_Write);
  and and_5 (and_5_out, Mask[3], Update_Mem, nRead_Write);
  RAM_part #(.addrWidth(16), .dataWidth(32), .bus("separate")) ram_1 (
    .addr(Address), .din(Data_In_0), .data(Data_Out_0), .str(and_2_out), .sel(Chip_Select), .clk(CLK),
    .ld(and_6_out), .clr(Reset));
  and and_6 (and_6_out, ~nRead_Write, Idle);  // AND_Gate
  RAM_part #(.addrWidth(16), .dataWidth(32), .bus("separate")) ram_2 (
    .addr(Address), .din(Data_In_1), .data(Data_Out_1), .str(and_3_out), .sel(Chip_Select), .clk(CLK),
    .ld(and_7_out), .clr(Reset));
  and and_7 (and_7_out, ~nRead_Write, Idle);  // AND_Gate
  RAM_part #(.addrWidth(16), .dataWidth(32), .bus("separate")) ram_3 (
    .addr(Address), .din(Data_In_2), .data(Data_Out_2), .str(and_4_out), .sel(Chip_Select), .clk(CLK),
    .ld(and_8_out), .clr(Reset));
  and and_8 (and_8_out, ~nRead_Write, Idle);  // AND_Gate
  RAM_part #(.addrWidth(16), .dataWidth(32), .bus("separate")) ram_4 (
    .addr(Address), .din(Data_In_3), .data(Data_Out_3), .str(and_5_out), .sel(Chip_Select), .clk(CLK),
    .ld(and_9_out), .clr(Reset));
  and and_9 (and_9_out, ~nRead_Write, Idle);  // AND_Gate

  assign Read_Time = 4'b0011;
  assign Write_Time = 4'b0010;

  // Other names for the same wires on the sheet: M0 = Mask[0]; M1 = Mask[1]; M2 = Mask[2]; M3 = Mask[3];
  //   RW = nRead_Write; CLR = Reset; CS = Chip_Select; Load2 = Count

  // Notes on the sheet:
  //   NO MODIFICAR
  //   excepto quizás los valores RT y WT
  //   BANK0
  //   BANK1
  //   BANK2
  //   BANK3
endmodule

module S_MIPS (
  input  Reset,
  input  [3:0] Read_Time,
  input  [31:0] RAM_Out_0,
  input  Clock,
  input  [3:0] Write_Time,
  input  Kbd_Available,
  input  [6:0] Kbd_ASCII_Data,
  input  [31:0] RAM_Out_1,
  input  [31:0] RAM_Out_2,
  input  [31:0] RAM_Out_3,
  output Kbd_Enable,
  output [31:0] RAM_In_0,
  output Kbd_Clear,
  output Stop,
  output [31:0] RAM_In_1,
  output [15:0] Address,
  output TTY_Enable,
  output [31:0] RAM_In_2,
  output [6:0] TTY_ASCII_Data,
  output nRead_Write,
  output Chip_Select,
  output [31:0] RAM_In_3,
  output [3:0] Mask
);


  // Other names for the same wires on the sheet: CLK = Clock; CLR = Reset; CS = Chip_Select;
  //   KBD_AVAIL = Kbd_Available; KBD_CLR = Kbd_Clear; KBD_DATA[6:0] = Kbd_ASCII_Data; RAM_A[15:0] = Address;
  //   RAM_INPUT_0[31:0] = RAM_In_0; RAM_INPUT_1[31:0] = RAM_In_1; RAM_INPUT_2[31:0] = RAM_In_2;
  //   RAM_INPUT_3[31:0] = RAM_In_3; RAM_MASK[3:0] = Mask; RAM_OUTPUT_0[31:0] = RAM_Out_0;
  //   RAM_OUTPUT_1[31:0] = RAM_Out_1; RAM_OUTPUT_2[31:0] = RAM_Out_2; RAM_OUTPUT_3[31:0] = RAM_Out_3;
  //   RW = nRead_Write; TTY_DATA[6:0] = TTY_ASCII_Data

  // Notes on the sheet:
  //   Inputs RAM
  //   DATA FROM RAM
  //   DATA WRITE MASK
  //   Outputs RAM
  //   RAM TIMING
  //   RAM ADDRESS
  //   RAM CONTROL
  //   DATA TO RAM
  //   Utilities
  //   KEYBOARD
  //   SEQUENCING
  //   TTY
endmodule

module RAM_Dispatcher (
  input  [3:0] WriteTime,
  input  Clock,
  input  CLR,
  output [31:0] Data,
  output [15:0] Address,
  output [3:0] Mask,
  output Finished,
  output Write
);

  wire demultiplexer_2_out1, demultiplexer_3_out1, End, IDLE_q, IncAddr, Load, or_1_out, or_2_out, While_q,
       WriteEnd;
  wire [3:0] counter_1_q;
  wire [31:0] CurrentAddress_q;

  Counter #(.width(32), .max('hffffffff)) CurrentAddress (
    .count(IncAddr), .Q({CurrentAddress_q[31:18], Address, CurrentAddress_q[1:0]}), .clk(Clock), .clr(CLR));  // open: load, D, carry
  or or_1 (or_1_out, IncAddr, demultiplexer_3_out1, Finished);
  D_Flip_Flop IDLE (.clk(Clock), .D(or_1_out), .Q(IDLE_q), .preset(CLR));  // open: Qn, en, reset
  Demultiplexer #(.enable("false")) demultiplexer_1 (.out0(Load), .out1(Finished), .in(IDLE_q), .sel(End));
  D_Flip_Flop While (.clk(Clock), .D(or_2_out), .Q(While_q), .reset(CLR));  // open: Qn, preset, en
  or or_2 (or_2_out, Write, Load);
  RAM_part #(.addrWidth(18), .dataWidth(32)) ram_1 (
    .addr({Address, CurrentAddress_q[1:0]}), .data(Data), .clk(Clock));  // open: sel, ld, clr
  Demultiplexer #(.enable("false")) demultiplexer_2 (
    .out0(Write), .out1(demultiplexer_2_out1), .in(While_q), .sel(WriteEnd));
  Decoder #(.select(2)) decoder_1 (
    .out0(Mask[0]), .out1(Mask[1]), .out2(Mask[2]), .out3(Mask[3]), .sel(CurrentAddress_q[1:0]));  // open: en
  Demultiplexer #(.enable("false")) demultiplexer_3 (
    .out0(IncAddr), .out1(demultiplexer_3_out1), .in(demultiplexer_2_out1), .sel(End));
  Counter #(.width(4), .max('hf)) counter_1 (
    .load(Load), .D(WriteTime), .count(Write), .Q(counter_1_q), .clk(Clock));  // open: carry, clr
  Comparator #(.width(32)) comparator_1 (.a(Data), .b({32{1'b1}}), .eq(End));  // open: gt, lt
  Comparator #(.width(4)) comparator_2 (.a(4'b0000), .b(counter_1_q), .eq(WriteEnd));  // open: gt, lt

  // Other names for the same wires on the sheet: CLK = Clock; Count = Write; WT[3:0] = WriteTime
endmodule

module Datapath (
  input  write_PC,
  input  Logical_Inmed_Op,
  input  [4:0] RS,
  input  [31:0] Data,
  input  [15:0] Offset,
  input  R_W,
  input  [1:0] select_B,
  input  [4:0] RT,
  input  [31:0] RT_2,
  input  [31:0] From_PC,
  input  rt_rd,
  input  [4:0] RD,
  input  clk,
  input  [3:0] ALU_Op,
  input  Push,
  input  reset,
  input  [2:0] Select_DI,
  input  Pop,
  input  [31:0] add_lw_sw,
  input  [31:0] RS_2,
  input  [31:0] To_PC,
  input  [31:0] SP,
  input  [31:0] Const,
  input  KBD_Available,
  input  [6:0] KBD_Data,
  output ZF,
  output NF
);

  wire [4:0] multiplexer_3_out;
  wire [31:0] ALU_Out, bit_extender_1_out, Hi, Lo, multiplexer_1_out, multiplexer_4_out, Random_out, RF_In,
       tunnel, undriven;

  assign bit_extender_1_out = {{25{1'b0}}, KBD_Data};  // Bit_Extender bit_extender_1
  Multiplexer #(.width(32), .enable("false")) multiplexer_1 (
    .in0({32{1'b1}}), .in1(bit_extender_1_out), .out(multiplexer_1_out), .sel(KBD_Available));
  Random #(.width(32), .seed(212)) Random (.clk(clk), .out(Random_out), .clr(reset));  // open: next
  Multiplexer #(.select(3), .width(32), .enable("false")) multiplexer_2 (
    .in0(add_lw_sw), .in1(Data), .in2(Hi), .in3(Lo), .in4(multiplexer_1_out), .in5(Random_out), .out(RF_In),
    .sel(Select_DI));  // open: in6, in7
  Register #(.width(32)) PC (.D(To_PC), .en(write_PC), .Q(From_PC), .clk(clk), .clr(reset));
  Multiplexer #(.width(5), .enable("false")) multiplexer_3 (.in0(RT), .in1(RD), .out(multiplexer_3_out), .sel(rt_rd));
  Register_File_2 register_file_1 (
    .in_1(multiplexer_3_out), .in_2(RF_In), .RW(R_W), .SA(RS), .SB(RT), .in_7(reset), .in_9(Pop), .in_6(clk),
    .in_8(Push), .A(RS_2), .B(RT_2), .SP(SP));
  Multiplexer #(.select(2), .width(32), .enable("false")) multiplexer_4 (
    .in0(RT_2), .in1(undriven), .in2(Const), .in3(tunnel), .out(multiplexer_4_out), .sel(select_B));
  ALU_2 alu_1 (.A(RS_2), .B(multiplexer_4_out), .ALU(ALU_Op), .Out(ALU_Out), .Zero(ZF), .Negative(NF));  // open: Hi, Lo
  Register #(.width(32)) u_Hi ();  // open: D, en, Q, clk, clr
  Register #(.width(32)) u_Lo ();  // open: D, en, Q, clk, clr
  ALU_2 alu_2 ();  // open: A, B, ALU, Out, Zero, Negative, Hi, Lo

  // Other names for the same wires on the sheet: ALU_out_t[31:0] = add_lw_sw; Data_In[31:0] = Data;
  //   KBD_A = KBD_Available; KBD_D[6:0] = KBD_Data; RS_t[31:0] = RS_2; rst = reset; RT_t[31:0] = RT_2

  // Notes on the sheet:
  //   Data From RAM
  //   RF Input Selecter
  //   Inputs
  //   CU Sings
  //   Program Counter
  //   From Instruction Decoder
  //   From Branch Control
  //   Data From KBD
  //   Data To RAM
  //   Outputs
  //   Data To RAM
endmodule

module ALU_2 (
  input  [31:0] Out,
  input  [31:0] A,
  input  [31:0] B,
  input  [3:0] ALU,
  input  [31:0] Hi,
  input  [31:0] Lo,
  output Zero,
  output Negative
);

  wire comparator_1_lt, comparator_2_lt;
  wire [31:0] AND, D_Hi, D_Lo, DIV_Hi, DIV_Lo, M_Hi, M_Lo, MULT_Hi, MULT_Lo, NOR, OR, tunnel, tunnel_t,
       tunnel_t_t, tunnel_t_t_t, XOR;

  // Probe on A
  // Probe on B
  Adder #(.width(32)) adder_1 (.a(A), .b(B), .out(tunnel));  // open: cin, cout
  Subtractor #(.width(32)) subtractor_1 (.a(A), .b(B), .out(tunnel_t));  // open: bin, bout
  assign AND = A & B;  // AND_Gate and_1, 32 bits wide
  assign OR = A | B;  // OR_Gate or_1, 32 bits wide
  Multiplier_part #(.width(32)) multiplier_1 (.a(A), .b(B), .out(MULT_Lo), .cout(MULT_Hi));  // open: cin
  Multiplier multiplier_2 (.A(A), .B(B), .Hi(M_Lo), .Lo(M_Hi));
  assign NOR = ~(A | B);  // NOR_Gate nor_1, 32 bits wide
  assign XOR = A ^ B;  // XOR_Gate xor_1, 32 bits wide
  Comparator #(.width(32)) comparator_1 (.a(A), .b(B), .lt(comparator_1_lt));  // open: gt, eq
  Comparator #(.width(32)) comparator_2 (.a(A), .b(B), .lt(comparator_2_lt));  // open: gt, eq
  Divider_part #(.width(32)) divider_1 (.a(A), .b(B), .out(DIV_Lo), .rem(DIV_Hi));  // open: upper
  Divider divider_2 (.A(A), .B(B), .Hi(D_Lo));  // open: Lo
  Multiplexer #(.width(32), .enable("false")) multiplexer_1 (
    .in0({32{1'b0}}), .in1(32'h1), .out(tunnel_t_t), .sel(comparator_1_lt));
  Multiplexer #(.width(32), .enable("false")) multiplexer_2 (
    .in0({32{1'b0}}), .in1(32'h1), .out(tunnel_t_t_t), .sel(comparator_2_lt));
  Multiplexer #(.select(3), .width(32), .enable("false")) multiplexer_3 (
    .in2(AND), .in3(OR), .in4(NOR), .in5(XOR), .in6(tunnel_t_t), .in7(tunnel_t_t_t), .out(Out), .sel(ALU[2:0]));  // open: in0, in1
  Multiplexer #(.select(2), .width(32), .enable("false")) multiplexer_4 (
    .in0(MULT_Hi), .in1(M_Hi), .in2(DIV_Hi), .in3(D_Hi), .out(Hi), .sel(ALU[1:0]));
  Multiplexer #(.select(2), .width(32), .enable("false")) multiplexer_5 (
    .in0(MULT_Lo), .in1(M_Lo), .in2(DIV_Lo), .in3(D_Lo), .out(Lo), .sel(ALU[1:0]));
  // Probe on Out
  // Probe on Hi
  // Probe on Lo
  Comparator #(.width(32)) comparator_3 (.a(Out), .b({32{1'b0}}), .eq(Zero));  // open: gt, lt

  assign Negative = Out[31];

  // Other names for the same wires on the sheet: O[2:0] = ALU[2:0]; O_Hi_Lo[1:0] = ALU[1:0]

  // Notes on the sheet:
  //   Operand A
  //   Operand B
  //   Inputs
  //   ALU Control
  //   Basic Operations
  //   Hi/Lo Operations
  //   Multiplier
  //   ALU
  //   Adder
  //   Substractor
  //   AND
  //   OR
  //   NOR
  //   XOR
  //   Comparator
  //   Divider
  //   Hi/Lo Outputs
  //   Outputs
  //   Normal
  //   SubCircuits
endmodule

module Multiplier (
  input  [31:0] A,
  input  [31:0] B,
  input  [31:0] Hi,
  input  [31:0] Lo
);

  wire In;
  wire [31:0] _00_Hi, _00_Lo, _01_Hi, _01_Lo, _10_Hi, _10_Lo, _11_Hi, _11_Lo, bit_extender_1_out,
       bit_extender_2_out, multiplier_3_cout, multiplier_3_out, multiplier_4_cout, multiplier_4_out,
       nand_1_out, nand_2_out, nand_3_out, nand_4_out, negator_1_out, negator_2_out, negator_3_out,
       negator_4_out;

  // Probe on A
  // Probe on B
  Multiplexer #(.select(2), .width(32), .enable("false")) multiplexer_1 (
    .in0(_00_Hi), .in1(_01_Hi), .in2(_10_Hi), .in3(_11_Hi), .out(Hi), .sel({A[31], B[31]}));
  Multiplexer #(.select(2), .width(32), .enable("false")) multiplexer_2 (
    .in0(_00_Lo), .in1(_01_Lo), .in2(_10_Lo), .in3(_11_Lo), .out(Lo), .sel({A[31], B[31]}));
  Multiplier_part #(.width(32)) multiplier_1 (.a(A), .b(B), .out(_00_Lo), .cout(_00_Hi));  // open: cin
  Negator #(.width(32)) negator_1 (.in(A), .out(negator_1_out));
  Multiplier_part #(.width(32)) multiplier_2 (
    .a(negator_1_out), .b(negator_2_out), .out(_11_Lo), .cout(_11_Hi));  // open: cin
  Negator #(.width(32)) negator_2 (.in(B), .out(negator_2_out));
  Multiplier_part #(.width(32)) multiplier_3 (
    .a(A), .b(negator_3_out), .out(multiplier_3_out), .cout(multiplier_3_cout));  // open: cin
  Negator #(.width(32)) negator_3 (.in(B), .out(negator_3_out));
  Multiplier_part #(.width(32)) multiplier_4 (
    .a(B), .b(negator_4_out), .out(multiplier_4_out), .cout(multiplier_4_cout));  // open: cin
  Negator #(.width(32)) negator_4 (.in(A), .out(negator_4_out));
  assign nand_1_out = ~(multiplier_3_out & {32{1'b1}});  // NAND_Gate nand_1, 32 bits wide
  assign nand_2_out = ~(multiplier_3_cout & {32{1'b1}});  // NAND_Gate nand_2, 32 bits wide
  assign nand_3_out = ~(multiplier_4_out & {32{1'b1}});  // NAND_Gate nand_3, 32 bits wide
  assign nand_4_out = ~(multiplier_4_cout & {32{1'b1}});  // NAND_Gate nand_4, 32 bits wide
  assign bit_extender_1_out = {{31{1'b0}}, In};  // Bit_Extender bit_extender_1
  assign bit_extender_2_out = {{31{1'b0}}, In};  // Bit_Extender bit_extender_2
  Adder #(.width(32)) adder_1 (.a(nand_1_out), .b(32'h1), .out(_01_Lo), .cout(In));  // open: cin
  Adder #(.width(32)) adder_2 (.a(nand_2_out), .b(bit_extender_1_out), .out(_01_Hi));  // open: cin, cout
  Adder #(.width(32)) adder_3 (.a(nand_3_out), .b(32'h1), .out(_01_Lo));  // open: cin, cout
  Adder #(.width(32)) adder_4 (.a(nand_4_out), .b(bit_extender_2_out), .out(_01_Hi));  // open: cin, cout

  // Other names for the same wires on the sheet: A_t = A[31]; B_t = B[31]

  // Notes on the sheet:
  //   Operand A
  //   Operand B
  //   Inputs
  //   Outputs
  //   Multiplier +-
  //   A(+) ^ B(+)
  //   A(-) ^ B(-)
  //   Operations
  //   A(+) ^ B(-)
  //   A(-) ^ B(+)
endmodule

module Divider (
  input  [31:0] A,
  input  [31:0] B,
  input  [31:0] Hi,
  input  [31:0] Lo
);

  wire [31:0] _00_Hi, _00_Lo, _01_Hi, _01_Lo, _10_Hi, _10_Lo, _11_Hi, _11_Lo, negator_1_out, negator_2_out,
       negator_3_out, negator_4_out, undriven;

  // Probe on A
  // Probe on B
  Multiplexer #(.select(2), .width(32), .enable("false")) multiplexer_1 (
    .in0(_00_Hi), .in1(_01_Hi), .in2(_10_Hi), .in3(_11_Hi), .out(Hi), .sel({A[31], B[31]}));
  Multiplexer #(.select(2), .width(32), .enable("false")) multiplexer_2 (
    .in0(_00_Lo), .in1(_01_Lo), .in2(_10_Lo), .in3(_11_Lo), .out(Lo), .sel({A[31], B[31]}));
  Divider_part #(.width(32)) divider_1 (.a(A), .b(B), .out(_00_Lo), .rem(_00_Hi));  // open: upper
  Negator #(.width(32)) negator_1 (.in(A), .out(negator_1_out));
  Negator #(.width(32)) negator_2 (.in(B), .out(negator_2_out));
  Divider_part #(.width(32)) divider_2 (
    .a(negator_1_out), .b(negator_2_out), .out(_00_Lo), .rem(_00_Hi));  // open: upper
  Negator #(.width(32)) negator_3 (.in(B), .out(negator_3_out));
  Negator #(.width(32)) negator_4 (.in(A), .out(negator_4_out));
  Divider_part #(.width(32)) divider_3 (.a(A), .b(negator_3_out), .out(_00_Lo), .rem(_00_Hi));  // open: upper
  Divider_part #(.width(32)) divider_4 (.a(negator_4_out), .b(undriven), .out(_00_Lo), .rem(_00_Hi));  // open: upper

  // Other names for the same wires on the sheet: A_t = A[31]; B_t = B[31]

  // Notes on the sheet:
  //   Operand A
  //   Operand B
  //   Inputs
  //   Outputs
  //   Divider +-
  //   A(+) ^ B(+)
  //   A(-) ^ B(-)
  //   Operations
  //   A(+) ^ B(-)
  //   A(-) ^ B(+)
endmodule

module Register_File_2 (
  input  [4:0] in_1,
  input  [31:0] in_2,
  input  RW,
  input  [4:0] SA,
  input  [4:0] SB,
  input  in_6,
  input  in_7,
  input  in_8,
  input  in_9,
  output [31:0] A,
  output [31:0] B,
  output [31:0] SP
);

  wire _0, _4, _8, _12, _16, _20, _24, _28, or_1_out;
  wire [1:0] priority_encoder_1_out;
  wire [2:1] _28___31;
  wire [3:1] _0___3, _4___7, _8___11, _12___15, _16___19, _20___23, _24___27;
  wire [4:0] multiplexer_1_out;
  wire [31:0] adder_1_out, multiplexer_3_out, Q10, Re0, Re1, Re2, Re3, Re4, Re5, Re6, Re7, Re8, Re9, Re10,
       Re11, Re12, Re13, Re14, Re15, Re16, Re17, Re18, Re19, Re20, Re21, Re22, Re23, Re24, Re25, Re26, Re27,
       Re28, Re29, Re30, subtractor_1_out, undriven;

  Decoder #(.select(5)) decoder_1 (
    .out0(_0), .out1(_0___3[1]), .out2(_0___3[2]), .out3(_0___3[3]), .out4(_4), .out5(_4___7[1]),
    .out6(_4___7[2]), .out7(_4___7[3]), .out8(_8), .out9(_8___11[1]), .out10(_8___11[2]), .out11(_8___11[3]),
    .out12(_12), .out13(_12___15[1]), .out14(_12___15[2]), .out15(_12___15[3]), .out16(_16),
    .out17(_16___19[1]), .out18(_16___19[2]), .out19(_16___19[3]), .out20(_20), .out21(_20___23[1]),
    .out22(_20___23[2]), .out23(_20___23[3]), .out24(_24), .out25(_24___27[1]), .out26(_24___27[2]),
    .out27(_24___27[3]), .out28(_28), .out29(_28___31[1]), .out30(_28___31[2]), .out31(in_9),
    .sel(multiplexer_1_out), .en(1'b1));
  Multiplexer #(.width(5), .enable("false")) multiplexer_1 (
    .in0({5{1'b0}}), .in1(in_1), .out(multiplexer_1_out), .sel(RW));
  Multiplexer #(.select(5), .width(32), .enable("false")) multiplexer_2 (
    .in0(Re0), .in1(Re1), .in2(Re2), .in3(Re3), .in4(Re4), .in5(Re5), .in6(Re6), .in7(Re7), .in8(Re8),
    .in9(Re9), .in10(Re10), .in11(Re11), .in12(Re12), .in13(Re13), .in14(Re14), .in15(Re15), .in16(Re16),
    .in17(Re17), .in18(Re18), .in19(Re19), .in20(Re20), .in21(Re21), .in22(Re22), .in23(Re23), .in24(Re24),
    .in25(Re25), .in26(Re26), .in27(Re27), .in28(Re28), .in29(Re29), .in30(Re30), .in31(SP), .out(A), .sel(SA));
  Register #(.width(32)) register_1 (.D(in_2), .en(_0___3[1]), .Q(Re1), .clk(in_6), .clr(in_7));
  Register #(.width(32)) register_2 (.D(in_2), .en(_4___7[3]), .Q(Re7), .clk(in_6), .clr(in_7));
  Register #(.width(32)) register_3 (.D(in_2), .en(_12___15[1]), .Q(Re13), .clk(in_6), .clr(in_7));
  Register #(.width(32)) register_4 (.D(in_2), .en(_16___19[3]), .Q(Re19), .clk(in_6), .clr(in_7));
  Register #(.width(32)) register_5 (.D(in_2), .en(_24___27[1]), .Q(Re25), .clk(in_6), .clr(in_7));
  Adder #(.width(32)) adder_1 (.a(SP), .b(32'h4), .out(adder_1_out));  // open: cin, cout
  Subtractor #(.width(32)) subtractor_1 (.a(SP), .b(32'h4), .out(subtractor_1_out));  // open: bin, bout
  Register #(.width(32)) register_6 (.D(in_2), .en(_0___3[2]), .Q(Re2), .clk(in_6), .clr(in_7));
  Register #(.width(32)) register_7 (.D(in_2), .en(_8), .Q(Re8), .clk(in_6), .clr(in_7));
  Register #(.width(32)) register_8 (.D(in_2), .en(_12___15[2]), .Q(Re14), .clk(in_6), .clr(in_7));
  Register #(.width(32)) register_9 (.D(in_2), .en(_20), .Q(Re20), .clk(in_6), .clr(in_7));
  Register #(.width(32)) register_10 (.D(in_2), .en(_24___27[2]), .Q(Re26), .clk(in_6), .clr(in_7));
  Multiplexer #(.select(2), .width(32), .enable("false")) multiplexer_3 (
    .in0(in_2), .in1(adder_1_out), .in2(subtractor_1_out), .in3(32'h3ffff), .out(multiplexer_3_out),
    .sel(priority_encoder_1_out));
  Priority_Encoder #(.select(2)) priority_encoder_1 (
    .in0(1'b1), .in1(in_9), .in2(in_8), .in3(in_7), .out(priority_encoder_1_out));
  Register #(.width(32)) R31__Stack_Pointer (.D(multiplexer_3_out), .en(or_1_out), .Q(SP), .clk(in_6));  // open: clr
  or or_1 (or_1_out, in_9, in_9, in_8, in_7);
  Register #(.width(32)) register_11 (.D(in_2), .en(_0___3[3]), .Q(Re3), .clk(in_6), .clr(in_7));
  Register #(.width(32)) register_12 (.D(in_2), .en(_8___11[1]), .Q(Re9), .clk(in_6), .clr(in_7));
  Register #(.width(32)) register_13 (.D(in_2), .en(_12___15[3]), .Q(Re15), .clk(in_6), .clr(in_7));
  Register #(.width(32)) register_14 (.D(in_2), .en(_20___23[1]), .Q(Re21), .clk(in_6), .clr(in_7));
  Register #(.width(32)) register_15 (.D(in_2), .en(_24___27[3]), .Q(Re27), .clk(in_6), .clr(in_7));
  Register #(.width(32)) register_16 (.D(in_2), .en(_4), .Q(Re4), .clk(in_6), .clr(in_7));
  Register #(.width(32)) register_17 (.D(in_2), .en(_8___11[2]), .Q(Re10), .clk(in_6), .clr(in_7));
  Register #(.width(32)) register_18 (.D(in_2), .en(_16), .Q(Re16), .clk(in_6), .clr(in_7));
  Register #(.width(32)) register_19 (.D(in_2), .en(_20___23[2]), .Q(Re22), .clk(in_6), .clr(in_7));
  Register #(.width(32)) register_20 (.D(in_2), .en(_28), .Q(Re28), .clk(in_6), .clr(in_7));
  Multiplexer #(.select(5), .width(32), .enable("false")) multiplexer_4 (
    .in0(Re0), .in1(Re1), .in2(Re2), .in3(Re3), .in4(Re4), .in5(Re5), .in6(Re6), .in7(Re7), .in8(Re8),
    .in9(Re9), .in10(Q10), .in11(Re11), .in12(Re12), .in13(Re13), .in14(Re14), .in15(Re15), .in16(Re16),
    .in17(Re17), .in18(Re18), .in19(Re19), .in20(Re20), .in21(undriven), .in22(Re22), .in23(Re23),
    .in24(Re24), .in25(Re25), .in26(Re26), .in27(Re27), .in28(Re28), .in29(Re29), .in30(Re30), .in31(SP),
    .out(B), .sel(SB));
  Register #(.width(32)) register_21 (.D(in_2), .en(_4___7[1]), .Q(Re5), .clk(in_6), .clr(in_7));
  Register #(.width(32)) register_22 (.D(in_2), .en(_8___11[3]), .Q(Re11), .clk(in_6), .clr(in_7));
  Register #(.width(32)) register_23 (.D(in_2), .en(_16___19[1]), .Q(Re17), .clk(in_6), .clr(in_7));
  Register #(.width(32)) register_24 (.D(in_2), .en(_20___23[3]), .Q(Re23), .clk(in_6), .clr(in_7));
  Register #(.width(32)) register_25 (.D(in_2), .en(_28___31[1]), .Q(Re29), .clk(in_6), .clr(in_7));
  Register #(.width(32)) R0 (.D({32{1'b0}}), .Q(Re0), .clk(in_6), .clr(in_7));  // open: en
  Register #(.width(32)) register_26 (.D(in_2), .en(_4___7[2]), .Q(Re6), .clk(in_6), .clr(in_7));
  Register #(.width(32)) register_27 (.D(in_2), .en(_12), .Q(Re12), .clk(in_6), .clr(in_7));
  Register #(.width(32)) register_28 (.D(in_2), .en(_16___19[2]), .Q(Re18), .clk(in_6), .clr(in_7));
  Register #(.width(32)) register_29 (.D(in_2), .en(_24), .Q(Re24), .clk(in_6), .clr(in_7));
  Register #(.width(32)) register_30 (.D(in_2), .en(_28___31[2]), .Q(Re30), .clk(in_6), .clr(in_7));

  // Other names for the same wires on the sheet: _0___3[0] = _0; _1 = _0___3[1]; _2 = _0___3[2]; _3 = _0___3[3];
  //   _4___7[0] = _4; _5 = _4___7[1]; _6 = _4___7[2]; _7 = _4___7[3]; _8___11[0] = _8; _9 = _8___11[1];
  //   _10 = _8___11[2]; _11 = _8___11[3]; _12___15[0] = _12; _13 = _12___15[1]; _14 = _12___15[2]; _15 = _12___15[3];
  //   _16___19[0] = _16; _17 = _16___19[1]; _18 = _16___19[2]; _19 = _16___19[3]; _20___23[0] = _20;
  //   _21 = _20___23[1]; _22 = _20___23[2]; _23 = _20___23[3]; _24___27[0] = _24; _25 = _24___27[1];
  //   _26 = _24___27[2]; _27 = _24___27[3]; _28___31 (some bits) = {in_9, _28}; _29 = _28___31[1]; _30 = _28___31[2];
  //   _31 = in_9; Pop = in_9; Address[4:0] = in_1; clock = in_6; Data_A[31:0] = A; Data_B[31:0] = B;
  //   Data_input[31:0] = in_2; Push = in_8; Re31[31:0] = SP; rst = in_7; Selected_A[4:0] = SA; Selected_B[4:0] = SB

  // Notes on the sheet:
  //   Outputs
  //   Stack Pointer
  //   Inputs
  //   Read/Write
  //   Selectors
  //   Data A
  //   Data B
  //   Writing Controller
  //   Load Tunnels
  //   Reading Controllers
  //   Stack Pointer
  //   Registers (1-30)
  //   Register 0
endmodule
